# Fritzing sketch schematic (saved by Fritzing 0.9.3b)
breadboards: 1

parts:
  Raspberry_Pi_1 = Raspberry Pi 3 [part_number=RPI-3-V1.2]
  Part1 = Arduino Uno (Rev3)
  S1 = Pushbutton [package="[THT]"]
  R1 = Resistor [tolerance=±5% resistance=220 package="0603 [SMD]"]
  LED1 = smd LED [color="Red (633nm)" package="1206 [SMD]"]
  U1 = TMP36 [package=to-92-kit]

nets:
  N1: Raspberry_Pi_1.GPIO17, S1.Pin_3, S1.Pin_4, R1.Pin_1, LED1.anode
  GND: Raspberry_Pi_1.GND, LED1.cathode, U1.GND
  5V: Raspberry_Pi_1.5V, U1.VCC
  N2: Part1.A0, U1.VOUT
  N3: S1.Pin_1, S1.Pin_2
